// Logisim project cpu.circ as structural Verilog: 1 circuit, main circuit main
module main (
  input  in_1
);

  wire clock_1_out, clock_2_out, decoder_1_out0, decoder_1_out1, decoder_1_out4, decoder_1_out5, MEM_READ,
       MEM_WRITE, MUX_2, MUX_3, MUX_IMM, or_1_out, PC_ADRESS, undriven_2;
  wire [3:0] ALU_OP;
  wire [15:0] alu_main_1_s, bit_extender_1_out, bit_extender_2_out, multiplexer_1_out, multiplexer_2_out,
       multiplexer_3_out, ram_1_dout, reg_file_1_a, reg_file_1_b, rom_1_data, undriven;

  PC_Main pc_main_1 (
    .PC_Src(PC_ADRESS), .Adress_Out(undriven), .Adress_Write(multiplexer_2_out));  // open: JR_Enable, Halt, CLK, JR_Adress, Reset
  ROM #(.addrWidth(16), .dataWidth(16)) rom_1 (.addr(undriven), .data(rom_1_data));
  Decoder #(.select(4)) decoder_1 (
    .out0(decoder_1_out0), .out1(decoder_1_out1), .out4(decoder_1_out4), .out5(decoder_1_out5),
    .sel(rom_1_data[15:12]), .en(in_1));  // open: out2, out3, out6, out7, out8, out9, out10, out11, out12, out13, out14, out15
  or or_1 (or_1_out, decoder_1_out0, decoder_1_out1, decoder_1_out4, decoder_1_out5);
  // OR_Gate or_2 is placed but not wired
  // OR_Gate or_3 is placed but not wired
  // OR_Gate or_4 is placed but not wired
  // OR_Gate or_5 is placed but not wired
  // OR_Gate or_6 is placed but not wired
  Clock clock_1 (.out(clock_1_out));
  assign bit_extender_1_out = {{12{rom_1_data[11]}}, rom_1_data[11:8]};  // Bit_Extender bit_extender_1
  assign bit_extender_2_out = {{4{rom_1_data[11]}}, rom_1_data[11:0]};  // Bit_Extender bit_extender_2
  REG_File reg_file_1 (
    .Reset(undriven_2), .Reg_Sel_A(rom_1_data[7:4]), .Reg_Sel_B(rom_1_data[3:0]), .Write_Enable(or_1_out),
    .Write_Reg(rom_1_data[11:8]), .Write_Data(multiplexer_2_out), .CLK(clock_1_out), .A(reg_file_1_a),
    .B(reg_file_1_b));
  Multiplexer #(.width(16)) multiplexer_1 (
    .in0(bit_extender_1_out), .in1(bit_extender_2_out), .out(multiplexer_1_out), .sel(MUX_IMM));
  Multiplexer #(.width(16)) multiplexer_2 (.in0(ram_1_dout), .in1(alu_main_1_s), .out(multiplexer_2_out), .sel(MUX_3));
  Multiplexer #(.width(16)) multiplexer_3 (
    .in0(reg_file_1_b), .in1(multiplexer_1_out), .out(multiplexer_3_out), .sel(MUX_2));
  ALU_Main alu_main_1 (
    .A(reg_file_1_a), .B(multiplexer_3_out), .ALU_Control(ALU_OP), .S(alu_main_1_s));  // open: N, C, Z, V
  RAM #(.addrWidth(16), .dataWidth(16)) ram_1 (
    .addr(alu_main_1_s), .we(MEM_WRITE), .oe(MEM_READ), .clk(clock_2_out), .din(reg_file_1_b),
    .dout(ram_1_dout));
  Clock clock_2 (.out(clock_2_out));

  // Notes on the sheet:
  //   REG_WRITE_ENABLE
  //   ALU_SRC
  //   MEM_READ
  //   MEM_WRITE
  //   MEM_TO_REG
  //   PC_ADRESS
  //   M2
endmodule
